# Fritzing sketch PushButtons (saved by Fritzing 0.9.2b)
breadboards: 1

parts:
  Raspberry_Pi1 = Raspberry Pi 2
  S1 = Momentary Switch [package=ksa_sealed_tac_switch]
  S2 = Momentary Switch [package=ksa_sealed_tac_switch]
  R1 = Resistor [tolerance=±5% resistance=4.7k package=THT]
  R2 = Resistor [tolerance=±5% resistance=4.7k package=THT]

nets:
  N1: Raspberry_Pi1.3v3, S1.4, S2.2
  N2: Raspberry_Pi1.GPIO17, S1.2
  N3: Raspberry_Pi1.GPIO18, S2.4
  N4: Raspberry_Pi1.GND, R1.Pin_0, R2.Pin_1
  N5: S1.1, R1.Pin_1
  N6: S2.3, R2.Pin_0
